# Fritzing sketch RADESP8266 (saved by Fritzing 0.9.3b)
breadboards: 1

parts:
  Part2 = FTDI Basic Programmer
  U2 = ESP8266 WiFi Module [part_number=ESP8266]
  LED = LED - 5mm [color="Red (633nm)" package="5 mm [THT]"]
  Switch_Button = Pushbutton [package="[THT]"]
  R1 = Resistor [tolerance=±5% resistance=10k package=THT]
  R2 = Resistor [tolerance=±5% resistance=220 package=THT]
  R3 = Resistor [tolerance=±5% resistance=10k package=THT]
  R4 = Resistor [tolerance=±5% resistance=10k package=THT]
  Reset_Button = Pushbutton [package="[THT]"]

nets:
  N1: Part2.RXI, U2.TXD
  N2: Part2.TXO, U2.RXD
  GND: Part2.GND, U2.GND, Switch_Button.Pin_3, Switch_Button.Pin_4, Reset_Button.Pin_3, Reset_Button.Pin_4
  3.3V: U2.VCC, U2.CH_PD, R1.Pin_0, R2.Pin_0, R3.Pin_0, R4.Pin_0
  N3: U2.GPIO_0, Switch_Button.Pin_1, Switch_Button.Pin_2, R3.Pin_1
  N4: U2.RST, R4.Pin_1, Reset_Button.Pin_1, Reset_Button.Pin_2
  N5: U2.GPIO_2, LED.cathode, R1.Pin_1
  N6: LED.anode, R2.Pin_1

custom parts:
  ESP8266 WiFi Module: Generic WiFi Module based on the ESP8266 with onboard PCB antenna and UART communications
